# Fritzing sketch schematic (saved by Fritzing 0.9.4)
breadboards: 2

parts:
  M1 = Stepper Motor - Bipolar
  Raspberry_Pi_1 = Raspberry Pi 3 [part_number=RPI-3-V1.2]
  Mod1 = KY-024 Linear Hall Magnetic Sensor Module [package="Breakout board"]
  LED1 = LEDs [package=led10mm]
  RY1 = KF-301 Relay [package=THT]
  Pololu_A2 = Pololu A4988 [package=SO16]  # not connected
  Part1 = 42CH Stepper Extension Board
  Part4 = USB-C PD Trigger Board
  M2 = RioRand LM2596
  JP1 = USB_MICROB_PLUG [package=micro-b-smt]
  M3 = RioRand LM2596
  F2 = Small Fan, based on Fan - Ventilador [package=THT]

nets:
  N1: M1.A, Part1.2B
  N2: M1.C, Part1.2A
  N3: M1.B, Part1.1B
  N4: M1.D, Part1.1A
  3V3: Raspberry_Pi_1.3v3, Raspberry_Pi_1.3V3, Part1.DIR-V, F2.5V
  GND: Raspberry_Pi_1.GND, Part1.DIR-G, F2.GND
  N5: Raspberry_Pi_1.GIPO6, RY1.signal
  N6: Raspberry_Pi_1.GIPO26, Mod1.D0
  N7: Raspberry_Pi_1.GIPO21, RY1.power, RY1.ground, Part1.DIR-S, Part1.STEP-V, Part1.STEP-G
  N8: Raspberry_Pi_1.GIPO20, Mod1.G, Part1.STEP-S, Part1.EN-G
  N9: Raspberry_Pi_1.GIPO16, Part1.EN-S
  N10: Mod1.+, Part1.EN-V
  N11: LED1.C, RY1.NC
  N12: LED1.A, Part1.GND, M3.Pin_4
  N13: RY1.C, Part1.VIN, M3.Pin_3
  N14: Part4.VOUT, M2.Pin_1, M3.Pin_1
  N15: Part4.GND, M2.Pin_2, M3.Pin_2
  N16: M2.Pin_3, JP1.VCC
  N17: M2.Pin_4, JP1.GND

notes:
  15V
  5V
  12V

custom parts:
  KY-024 Linear Hall Magnetic Sensor Module: KY-024 Linear Hall Magnetic Sensor Module reacts iin the presence of a magnetic field.
  KF-301 Relay: KF-301 SPDT Relay module using SRD-05VDC-SL-C relay.
  42CH Stepper Extension Board: Jolicobo 3D Printer 42CH Schrittmotortreiber Abchirmung Erweiterungskarte DRV8825 / A4988 UNO R3 (Schwarz)
  Small Fan, based on Fan - Ventilador: Small 2-pin fan, commonly used with single-board computers, 3d-printers, etc. This work is based on a much larger fan, as commonly found in desktop computers
