# Fritzing sketch schematic_upgrade (saved by Fritzing 0.9.4)

parts:
  M1 = Stepper Motor - Bipolar
  Raspberry_Pi_1 = Raspberry Pi 3 [part_number=RPI-3-V1.2]
  Mod1 = KY-024 Linear Hall Magnetic Sensor Module [package="Breakout board"]
  LED1 = LEDs [package=led10mm]
  RY1 = KF-301 Relay [package=THT]
  Pololu_A2 = Pololu A4988 [package=SO16]  # not connected
  Part1 = 42CH Stepper Extension Board
  Part4 = USB-C PD Trigger Board
  M2 = RioRand LM2596
  JP1 = USB_MICROB_PLUG [package=micro-b-smt]
  M3 = RioRand LM2596
  Part5 = TXB0108 8-channel Bi-directional Logic Level Converter

nets:
  N1: M1.A, Part1.2B
  N2: M1.C, Part1.2A
  N3: M1.B, Part1.1B
  N4: M1.D, Part1.1A
  3V3: Raspberry_Pi_1.3v3, Raspberry_Pi_1.3V3, Mod1.+, Part1.DIR-V
  GND: Raspberry_Pi_1.GND, Mod1.G, RY1.ground, Part1.DIR-G, Part5.GND
  N5: Raspberry_Pi_1.GIPO6, Part5.A1
  N6: Raspberry_Pi_1.GIPO26, Mod1.D0
  N7: Raspberry_Pi_1.GIPO21, Part1.DIR-S
  N8: Raspberry_Pi_1.GIPO20, Part1.STEP-S
  N9: Raspberry_Pi_1.GIPO16, Part1.EN-S
  N10: Raspberry_Pi_1.5V, RY1.power, Part5.VCCB
  N11: LED1.C, RY1.NC
  N12: LED1.A, M3.Pin_4
  N13: RY1.signal, Part5.B1
  N14: RY1.C, M3.Pin_3
  N15: Part1.VIN, Part4.VOUT, M2.Pin_1, M3.Pin_1
  GND_2: Part1.GND, Part4.GND, M2.Pin_2, M3.Pin_2
  N16: Part1.EN-V, Part5.VCCA
  N17: M2.Pin_3, JP1.VCC
  N18: M2.Pin_4, JP1.GND

notes:
  20V -> 12V
  (draws 3W / 0.25A)
  20V -> 5V
  (draws 2A / assume 3A / 15W)
  20V
  (assume it draws 1.5-3.0A / 30W to 60W ... or according to I^2 * R we get 10.35W (plus reserve)

custom parts:
  KY-024 Linear Hall Magnetic Sensor Module: KY-024 Linear Hall Magnetic Sensor Module reacts iin the presence of a magnetic field.
  KF-301 Relay: KF-301 SPDT Relay module using SRD-05VDC-SL-C relay.
  42CH Stepper Extension Board: Jolicobo 3D Printer 42CH Schrittmotortreiber Abchirmung Erweiterungskarte DRV8825 / A4988 UNO R3 (Schwarz)
  TXB0108 8-channel Bi-directional Logic Level Converter: Because the Arduino (and Basic Stamp) are 5V devices, and most modern sensors, displays, flash cards and modes are 3.3V-only, many makers find that they need to perform level shifting/conversion to protect the 3.3V device from 5V. Although one can use resistors to make a divider, for high speed transfers, the resistors can add a lot of slew and cause havoc that is tough to debug. For that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
